# Fritzing sketch hm-10_test_schematic (saved by Fritzing 0.9.3b)

parts:
  Part1 = Bluetooth HM-10
  Part2 = Arduino Nano (Rev3.0) (ICSP)
  LED2 = smd LED [color="Orange (620nm)" package="1206 [SMD]"]
  U1 = POT_SWITCH [package=pot_pth_switch]
  R1 = Resistor [tolerance=±5% resistance=330 package=THT]

nets:
  N1: Part1.RXD, Part2.D10
  GND: Part1.TXD, Part1.GND, Part2.GND, Part2.D9, U1.G$2_2
  VCC: Part1.VCC, Part2.5V, U1.G$1_A
  N2: Part2.D3, LED2.anode
  N3: Part2.A0, U1.G$2_1
  N4: LED2.cathode, R1.Pin_0
